// Logisim project ULA.circ as structural Verilog: 4 circuits, main circuit main
module main (
  input  [31:0] Entrada_A,
  input  [31:0] Entrada_B,
  input  [4:0] Seletor,
  output Overflow,
  output [31:0] \Saída_S 
);

  wire celulaula_1_cout, celulaula_2_cout, celulaula_3_cout, celulaula_4_cout, celulaula_5_cout,
       celulaula_6_cout, celulaula_7_cout, celulaula_8_cout, celulaula_9_cout, celulaula_10_cout,
       celulaula_11_cout, celulaula_12_cout, celulaula_13_cout, celulaula_14_cout, celulaula_15_cout,
       celulaula_16_cout, celulaula_17_cout, celulaula_18_cout, celulaula_19_cout, celulaula_20_cout,
       celulaula_21_cout, celulaula_22_cout, celulaula_23_cout, celulaula_25_cout, celulaula_26_cout,
       celulaula_28_cout, celulaula_29_cout, celulaula_30_cout, celulaula_31_cout, celulaula_32_cout,
       Overflow_overflow;

  CelulaULA celulaula_1 (
    .a(Entrada_A[30]), .b(Entrada_B[30]), .Cin(celulaula_2_cout), .Seletor(Seletor), .S(\Saída_S [1]),
    .Cout(celulaula_1_cout));
  CelulaULA celulaula_2 (
    .a(Entrada_A[31]), .b(Entrada_B[31]), .Cin(celulaula_4_cout), .Seletor(Seletor), .S(\Saída_S [0]),
    .Cout(celulaula_2_cout));
  CelulaULA celulaula_3 (
    .a(Entrada_A[28]), .b(Entrada_B[28]), .Cin(celulaula_1_cout), .Seletor(Seletor), .S(\Saída_S [3]),
    .Cout(celulaula_3_cout));
  CelulaULA celulaula_4 (
    .a(Entrada_A[29]), .b(Entrada_B[29]), .Cin(celulaula_6_cout), .Seletor(Seletor), .S(\Saída_S [2]),
    .Cout(celulaula_4_cout));
  CelulaULA celulaula_5 (
    .a(Entrada_A[26]), .b(Entrada_B[27]), .Cin(celulaula_3_cout), .Seletor(Seletor), .S(\Saída_S [5]),
    .Cout(celulaula_5_cout));
  CelulaULA celulaula_6 (
    .a(Entrada_A[27]), .b(Entrada_B[26]), .Cin(celulaula_8_cout), .Seletor(Seletor), .S(\Saída_S [4]),
    .Cout(celulaula_6_cout));
  CelulaULA celulaula_7 (
    .a(Entrada_A[24]), .b(Entrada_B[25]), .Cin(celulaula_5_cout), .Seletor(Seletor), .S(\Saída_S [7]),
    .Cout(celulaula_7_cout));
  CelulaULA celulaula_8 (
    .a(Entrada_A[25]), .b(Entrada_A[25]), .Cin(celulaula_10_cout), .Seletor(Seletor), .S(\Saída_S [6]),
    .Cout(celulaula_8_cout));
  CelulaULA celulaula_9 (
    .a(Entrada_A[22]), .b(Entrada_B[23]), .Cin(celulaula_7_cout), .Seletor(Seletor), .S(\Saída_S [9]),
    .Cout(celulaula_9_cout));
  CelulaULA celulaula_10 (
    .a(Entrada_A[23]), .b(Entrada_B[22]), .Cin(celulaula_12_cout), .Seletor(Seletor), .S(\Saída_S [8]),
    .Cout(celulaula_10_cout));
  CelulaULA celulaula_11 (
    .a(Entrada_A[20]), .b(Entrada_B[21]), .Cin(celulaula_9_cout), .Seletor(Seletor), .S(\Saída_S [11]),
    .Cout(celulaula_11_cout));
  CelulaULA celulaula_12 (
    .a(Entrada_A[21]), .b(Entrada_B[20]), .Cin(celulaula_14_cout), .Seletor(Seletor), .S(\Saída_S [10]),
    .Cout(celulaula_12_cout));
  CelulaULA celulaula_13 (
    .a(Entrada_A[18]), .b(Entrada_B[19]), .Cin(celulaula_11_cout), .Seletor(Seletor), .S(\Saída_S [13]),
    .Cout(celulaula_13_cout));
  CelulaULA celulaula_14 (
    .a(Entrada_A[19]), .b(Entrada_B[18]), .Cin(celulaula_16_cout), .Seletor(Seletor), .S(\Saída_S [12]),
    .Cout(celulaula_14_cout));
  CelulaULA celulaula_15 (
    .a(Entrada_A[16]), .b(Entrada_B[17]), .Cin(celulaula_13_cout), .Seletor(Seletor), .S(\Saída_S [15]),
    .Cout(celulaula_15_cout));
  CelulaULA celulaula_16 (
    .a(Entrada_A[17]), .b(Entrada_B[16]), .Cin(celulaula_18_cout), .Seletor(Seletor), .S(\Saída_S [14]),
    .Cout(celulaula_16_cout));
  CelulaULA celulaula_17 (
    .a(Entrada_A[14]), .b(Entrada_B[15]), .Cin(celulaula_15_cout), .Seletor(Seletor), .S(\Saída_S [17]),
    .Cout(celulaula_17_cout));
  CelulaULA celulaula_18 (
    .a(Entrada_A[15]), .b(Entrada_B[14]), .Cin(celulaula_20_cout), .Seletor(Seletor), .S(\Saída_S [16]),
    .Cout(celulaula_18_cout));
  CelulaULA celulaula_19 (
    .a(Entrada_A[12]), .b(Entrada_B[13]), .Cin(celulaula_17_cout), .Seletor(Seletor), .S(\Saída_S [19]),
    .Cout(celulaula_19_cout));
  CelulaULA celulaula_20 (
    .a(Entrada_A[13]), .b(Entrada_B[12]), .Cin(celulaula_22_cout), .Seletor(Seletor), .S(\Saída_S [18]),
    .Cout(celulaula_20_cout));
  CelulaULA celulaula_21 (
    .a(Entrada_A[10]), .b(Entrada_B[11]), .Cin(celulaula_19_cout), .Seletor(Seletor), .S(\Saída_S [21]),
    .Cout(celulaula_21_cout));
  CelulaULA celulaula_22 (
    .a(Entrada_A[11]), .b(Entrada_B[10]), .Cin(Entrada_B[10]), .Seletor(Seletor), .S(\Saída_S [20]),
    .Cout(celulaula_22_cout));
  CelulaULA celulaula_23 (
    .a(Entrada_A[8]), .b(Entrada_B[9]), .Cin(celulaula_21_cout), .Seletor(Seletor), .S(\Saída_S [23]),
    .Cout(celulaula_23_cout));
  CelulaULA celulaula_24 (
    .a(Entrada_A[9]), .b(Entrada_B[8]), .Cin(celulaula_26_cout), .Seletor(Seletor), .S(\Saída_S [22]),
    .Cout(Entrada_B[10]));
  CelulaULA celulaula_25 (
    .a(Entrada_A[6]), .b(Entrada_B[7]), .Cin(celulaula_23_cout), .Seletor(Seletor), .S(\Saída_S [25]),
    .Cout(celulaula_25_cout));
  CelulaULA celulaula_26 (
    .a(Entrada_A[7]), .b(Entrada_B[6]), .Cin(celulaula_28_cout), .Seletor(Seletor), .S(\Saída_S [24]),
    .Cout(celulaula_26_cout));
  CelulaULA celulaula_27 (
    .a(Entrada_A[4]), .b(Entrada_B[5]), .Cin(celulaula_25_cout), .Seletor(Seletor), .S(\Saída_S [27]),
    .Cout(Entrada_B[3]));
  CelulaULA celulaula_28 (
    .a(Entrada_A[5]), .b(Entrada_B[4]), .Cin(celulaula_30_cout), .Seletor(Seletor), .S(\Saída_S [26]),
    .Cout(celulaula_28_cout));
  CelulaULA celulaula_29 (
    .a(Entrada_A[2]), .b(Entrada_B[3]), .Cin(Entrada_B[3]), .Seletor(Seletor), .S(\Saída_S [29]),
    .Cout(celulaula_29_cout));
  CelulaULA celulaula_30 (
    .a(Entrada_A[3]), .b(Entrada_B[2]), .Cin(celulaula_32_cout), .Seletor(Seletor), .S(\Saída_S [28]),
    .Cout(celulaula_30_cout));
  CelulaULA celulaula_31 (
    .a(Entrada_A[0]), .b(Entrada_B[1]), .Cin(celulaula_29_cout), .Seletor(Seletor), .S(\Saída_S [31]),
    .Cout(celulaula_31_cout));
  CelulaULA celulaula_32 (
    .a(Entrada_A[1]), .b(Entrada_B[0]), .Cin(1'b0), .Seletor(Seletor), .S(\Saída_S [30]),
    .Cout(celulaula_32_cout));
  OverFlowControler u_Overflow (
    .Overflow(Overflow_overflow), .Cin(celulaula_31_cout), .Seletor(Seletor), .a(Entrada_A[0]),
    .b(Entrada_B[1]), .s(\Saída_S [31]));

  assign Entrada_B[24] = Entrada_A[25];

  // Notes on the sheet:
  //   00000=AND
  //   00001=OR
  //   00010=XOR
  //   00011=NAND
  //   00100=SOMA INT
  //   00101=SOMA NAT
endmodule

module Somador (
  input  a,
  input  b,
  input  Cin,
  output Cout,
  output s
);

  wire and_1_out, and_2_out, and_3_out, and_4_out, xor_2_out;

  xor xor_1 (s, Cin, xor_2_out);
  xor xor_2 (xor_2_out, a, b);
  and and_1 (and_1_out, ~Cin, a, b);  // AND_Gate
  and and_2 (and_2_out, Cin, ~a, b);  // AND_Gate
  and and_3 (and_3_out, Cin, a, ~b);  // AND_Gate
  and and_4 (and_4_out, Cin, a, b);
  or or_1 (Cout, and_1_out, and_2_out, and_3_out, and_4_out);
endmodule

// Celula
module CelulaULA (
  input  a,
  input  b,
  input  Cin,
  input  [4:0] Seletor,
  output S,
  output Cout
);

  wire and_1_out, nand_1_out, or_1_out, somador_1_s, xor_1_out;

  and and_1 (and_1_out, a, b);
  or or_1 (or_1_out, a, b);
  xor xor_1 (xor_1_out, a, b);
  nand nand_1 (nand_1_out, a, b);
  Somador somador_1 (.Cin(Cin), .a(b), .b(a), .s(somador_1_s), .Cout(Cout));
  Multiplexer #(.select(5), .enable("false")) multiplexer_1 (
    .in0(and_1_out), .in1(or_1_out), .in2(xor_1_out), .in3(nand_1_out), .in4(somador_1_s), .in5(somador_1_s),
    .out(S), .sel(Seletor));  // open: in6, in7, in8, in9, in10, in11, in12, in13, in14, in15, in16, in17, in18, in19, in20, in21, in22, in23, in24, in25, in26, in27, in28, in29, in30, in31

  // Notes on the sheet:
  //   00000=AND
  //   00001=OR
  //   00010=XOR
  //   00011=NAND
  //   00100=SOMA INT
  //   00101=SOMA NAT
endmodule

module OverFlowControler (
  input  Cin,
  input  a,
  input  b,
  input  s,
  input  [4:0] Seletor,
  output Overflow
);

  wire and_1_out, and_2_out, and_3_out, or_1_out;

  Multiplexer #(.enable("false")) multiplexer_1 (.in0(Cin), .out(Overflow), .sel(and_1_out));  // open: in1
  and and_1 (and_1_out, Seletor[0], ~Seletor[1], Seletor[2], ~Seletor[3], ~Seletor[4]);  // AND_Gate
  or or_1 (or_1_out, and_2_out, and_3_out);
  and and_2 (and_2_out, a, b, ~s);  // AND_Gate
  and and_3 (and_3_out, ~a, ~b, s);  // AND_Gate

  // Notes on the sheet:
  //   00100 - Soma de Naturais
  //   00101 - Soma de Inteiros
endmodule
